// Logisim project RISCV_Multiciclo.circ as structural Verilog: 12 circuits, main circuit main
module main (
  input  RESET,
  input  PCWriteCond,
  input  PCWrite,
  input  IorD,
  input  MemRead,
  input  MemWrite,
  input  MemToReg,
  input  IRWrite,
  input  RegWrite,
  input  [1:0] ALUsrcA,
  input  [1:0] ALUsrcB,
  input  [1:0] ALUop,
  input  PCSource,
  input  Manual,
  output [3:0] Estado,
  output PCWriteCond_2,
  output PCWrite_2,
  output IorD_2,
  output MemRead_2,
  output MemWrite_2,
  output MemtoReg_2,
  output IRWrite_2,
  output RegWrite_2,
  output [1:0] ALUSrcA_2,
  output [1:0] ALUSrcB_2,
  output [1:0] ALUop_2,
  output PCSource_2
);

  wire alu_1_zero, and_1_out, clock_1_out, or_1_out;
  wire [2:0] instruction_register_1_funct3;
  wire [3:0] alu_control_1_alucontrol;
  wire [4:0] instruction_register_1_rd, instruction_register_1_rs1, instruction_register_1_rs2;
  wire [6:0] instruction_register_1_funct7, instruction_register_1_opcode;
  wire [31:0] A_q, alu_1_out_5, ALU_Out_q, B_q, immgen_1_immediate, instruction_register_1_instruction,
       MDR_q, multiplexer_1_out, multiplexer_2_out, multiplexer_3_out, multiplexer_4_out, multiplexer_5_out,
       OldPC_q, PC_q, Post_ALU_final_address, ram_1_data, register_bank_1_read_data_1,
       register_bank_1_read_data_2, shifter_1_out;

  Clock clock_1 (.out(clock_1_out));
  Register #(.width(32)) PC (.D(multiplexer_5_out), .en(or_1_out), .Q(PC_q), .clk(clock_1_out), .clr(RESET));
  Multiplexer #(.width(32), .enable("false")) multiplexer_1 (
    .in0(PC_q), .in1(ALU_Out_q), .out(multiplexer_1_out), .sel(IorD_2));
  or or_1 (or_1_out, PCWrite_2, and_1_out);
  and and_1 (and_1_out, PCWriteCond_2, alu_1_zero);
  FSM_ROM fsm_rom_1 (
    .OPCode(instruction_register_1_opcode), .Clock(clock_1_out), .Reset(RESET), .PCWriteCond(PCWriteCond),
    .PCWrite(PCWrite), .IorD(IorD), .MemRead(MemRead), .MemWrite(MemWrite), .MemToReg(MemToReg),
    .IRWrite(IRWrite), .RegWrite(RegWrite), .ALUsrcA(ALUsrcA), .ALUsrcB(ALUsrcB), .ALUop(ALUop),
    .PCSource(PCSource), .Estado__debug(Estado), .Debug(Manual), .PCWriteCond_2(PCWriteCond_2),
    .PCWrite_2(PCWrite_2), .IorD_2(IorD_2), .MemRead_2(MemRead_2), .MemWrite_2(MemWrite_2),
    .MemtoReg_2(MemtoReg_2), .IRWrite_2(IRWrite_2), .RegWrite_2(RegWrite_2), .ALUSrcA_2(ALUSrcA_2),
    .ALUSrcB_2(ALUSrcB_2), .ALUop_2(ALUop_2), .PCSource_2(PCSource_2));
  RAM #(.addrWidth(24), .dataWidth(32), .bus("separate")) ram_1 (
    .addr(multiplexer_1_out[25:2]), .din(B_q), .data(ram_1_data), .str(MemWrite_2), .sel(1'b1),
    .clk(clock_1_out), .ld(MemRead_2), .clr(1'b0));
  Instruction_Register instruction_register_1 (
    .in_1(ram_1_data), .Enable(IRWrite_2), .Reset(RESET), .Clock(clock_1_out),
    .opcode(instruction_register_1_opcode), .rd(instruction_register_1_rd),
    .funct3(instruction_register_1_funct3), .rs1(instruction_register_1_rs1),
    .rs2(instruction_register_1_rs2), .funct7(instruction_register_1_funct7),
    .Instruction(instruction_register_1_instruction));
  Register #(.width(32)) MDR (.D(ram_1_data), .en(1'b1), .Q(MDR_q), .clk(clock_1_out), .clr(RESET));
  Register #(.width(32)) OldPC (.D(PC_q), .en(or_1_out), .Q(OldPC_q), .clk(clock_1_out), .clr(RESET));
  Multiplexer #(.width(32), .enable("false")) multiplexer_2 (
    .in0(ALU_Out_q), .in1(MDR_q), .out(multiplexer_2_out), .sel(MemtoReg_2));
  Register_Bank register_bank_1 (
    .Read_1_Address(instruction_register_1_rs1), .Read_2_Address(instruction_register_1_rs2),
    .Write_Address(instruction_register_1_rd), .Write_Data(multiplexer_2_out), .Enable(RegWrite_2),
    .Reset(RESET), .Clock(clock_1_out), .Read_Data_1(register_bank_1_read_data_1),
    .Read_Data_2(register_bank_1_read_data_2));
  ImmGen immgen_1 (.Instruction(instruction_register_1_instruction), .Immediate(immgen_1_immediate));
  Register #(.width(32)) A (.D(register_bank_1_read_data_1), .en(1'b1), .Q(A_q), .clk(clock_1_out), .clr(RESET));
  Register #(.width(32)) B (.D(register_bank_1_read_data_2), .en(1'b1), .Q(B_q), .clk(clock_1_out), .clr(RESET));
  Shifter #(.width(32)) shifter_1 (.in(immgen_1_immediate), .\dist (5'b00001), .out(shifter_1_out));
  Multiplexer #(.select(2), .width(32), .enable("false")) multiplexer_3 (
    .in0(PC_q), .in1(OldPC_q), .in2(A_q), .out(multiplexer_3_out), .sel(ALUSrcA_2));  // open: in3
  Multiplexer #(.select(2), .width(32), .enable("false")) multiplexer_4 (
    .in0(B_q), .in1(32'h4), .in2(immgen_1_immediate), .in3(shifter_1_out), .out(multiplexer_4_out),
    .sel(ALUSrcB_2));
  postALU Post_ALU (
    .ALU_Computed_Address(alu_1_out_5), .opcode(instruction_register_1_opcode),
    .Final_Address(Post_ALU_final_address));
  ALU alu_1 (
    .in_1(multiplexer_3_out), .in_2(multiplexer_4_out), .in_3(alu_control_1_alucontrol), .Zero(alu_1_zero),
    .out_5(alu_1_out_5));
  Register #(.width(32)) ALU_Out (.D(alu_1_out_5), .en(1'b1), .Q(ALU_Out_q), .clk(clock_1_out), .clr(RESET));
  ALU_Control alu_control_1 (
    .ALUOp(ALUop_2), .funct3(instruction_register_1_funct3), .funct7(instruction_register_1_funct7),
    .ALUControl(alu_control_1_alucontrol));
  Multiplexer #(.width(32), .enable("false")) multiplexer_5 (
    .in0(Post_ALU_final_address), .in1(ALU_Out_q), .out(multiplexer_5_out), .sel(PCSource_2));

  // Notes on the sheet:
  //   Bloco Operativo
  //   Bloco de Controle
  //   Memory
  //   IR
  //   LUI x5. 0x12345 -> x5 = 0x12345000
  //   ImmGen
  //   Reg. Bank
  //   ALU Control
  //   ALU
endmodule

module Instruction_Register (
  input  [31:0] in_1,
  input  Enable,
  input  Reset,
  input  Clock,
  output [6:0] opcode,
  output [4:0] rd,
  output [2:0] funct3,
  output [4:0] rs1,
  output [4:0] rs2,
  output [6:0] funct7,
  output [31:0] Instruction
);

  Register #(.width(32)) register_1 (
    .D(in_1), .en(Enable), .Q({funct7, Instruction[24:15], funct3, Instruction[11:0]}), .clk(Clock),
    .clr(Reset));

  assign {Instruction[31:25], Instruction[14:12]} = {funct7, funct3};
  assign opcode = Instruction[6:0];
  assign rd = Instruction[11:7];
  assign rs1 = Instruction[19:15];
  assign rs2 = Instruction[24:20];
endmodule

module Register_Bank (
  input  [4:0] Read_1_Address,
  input  [4:0] Read_2_Address,
  input  [4:0] Write_Address,
  input  [31:0] Write_Data,
  input  Enable,
  input  Reset,
  input  Clock,
  output [31:0] Read_Data_1,
  output [31:0] Read_Data_2
);

  wire and_1_out, and_2_out, and_3_out, and_4_out, and_5_out, and_6_out, and_7_out, and_8_out, and_9_out,
       and_10_out, and_11_out, and_12_out, and_13_out, and_14_out, and_15_out, and_16_out, and_17_out,
       and_18_out, and_19_out, and_20_out, and_21_out, and_22_out, and_23_out, and_24_out, and_25_out,
       and_26_out, and_27_out, and_28_out, and_29_out, and_30_out, and_31_out, and_32_out, dec_5_1_1_out_2,
       dec_5_1_1_out_3, dec_5_1_1_out_4, dec_5_1_1_out_5, dec_5_1_1_out_6, dec_5_1_1_out_7, dec_5_1_1_out_8,
       dec_5_1_1_out_9, dec_5_1_1_out_10, dec_5_1_1_out_11, dec_5_1_1_out_12, dec_5_1_1_out_13,
       dec_5_1_1_out_14, dec_5_1_1_out_15, dec_5_1_1_out_16, dec_5_1_1_out_17, dec_5_1_1_out_18,
       dec_5_1_1_out_19, dec_5_1_1_out_20, dec_5_1_1_out_21, dec_5_1_1_out_22, dec_5_1_1_out_23,
       dec_5_1_1_out_24, dec_5_1_1_out_25, dec_5_1_1_out_26, dec_5_1_1_out_27, dec_5_1_1_out_28,
       dec_5_1_1_out_29, dec_5_1_1_out_30, dec_5_1_1_out_31, dec_5_1_1_out_32, dec_5_1_1_out_33;
  wire [31:0] _2_q, _3_q, _4_q, _5_q, _6_q, _7_q, _8_q, _9_q, _10_q, _11_q, _12_q, _13_q, _14_q, _15_q,
       _16_q, _17_q, _18_q, _19_q, _20_q, _21_q, _22_q, _23_q, _24_q, _25_q, _26_q, _27_q, _28_q, _29_q,
       _30_q, _31_q, multiplexer_1_out, multiplexer_2_out, multiplexer_3_out, multiplexer_4_out, register_1_q;

  Dec_5_1 dec_5_1_1 (
    .in_1(Write_Address), .out_2(dec_5_1_1_out_2), .out_3(dec_5_1_1_out_3), .out_4(dec_5_1_1_out_4),
    .out_5(dec_5_1_1_out_5), .out_6(dec_5_1_1_out_6), .out_7(dec_5_1_1_out_7), .out_8(dec_5_1_1_out_8),
    .out_9(dec_5_1_1_out_9), .out_10(dec_5_1_1_out_10), .out_11(dec_5_1_1_out_11), .out_12(dec_5_1_1_out_12),
    .out_13(dec_5_1_1_out_13), .out_14(dec_5_1_1_out_14), .out_15(dec_5_1_1_out_15),
    .out_16(dec_5_1_1_out_16), .out_17(dec_5_1_1_out_17), .out_18(dec_5_1_1_out_18),
    .out_19(dec_5_1_1_out_19), .out_20(dec_5_1_1_out_20), .out_21(dec_5_1_1_out_21),
    .out_22(dec_5_1_1_out_22), .out_23(dec_5_1_1_out_23), .out_24(dec_5_1_1_out_24),
    .out_25(dec_5_1_1_out_25), .out_26(dec_5_1_1_out_26), .out_27(dec_5_1_1_out_27),
    .out_28(dec_5_1_1_out_28), .out_29(dec_5_1_1_out_29), .out_30(dec_5_1_1_out_30),
    .out_31(dec_5_1_1_out_31), .out_32(dec_5_1_1_out_32), .out_33(dec_5_1_1_out_33));
  and and_1 (and_1_out, dec_5_1_1_out_2, Enable);
  and and_2 (and_2_out, dec_5_1_1_out_3, Enable);
  and and_3 (and_3_out, dec_5_1_1_out_4, Enable);
  and and_4 (and_4_out, dec_5_1_1_out_5, Enable);
  and and_5 (and_5_out, dec_5_1_1_out_6, Enable);
  and and_6 (and_6_out, dec_5_1_1_out_7, Enable);
  and and_7 (and_7_out, dec_5_1_1_out_8, Enable);
  and and_8 (and_8_out, dec_5_1_1_out_9, Enable);
  and and_9 (and_9_out, dec_5_1_1_out_10, Enable);
  and and_10 (and_10_out, dec_5_1_1_out_11, Enable);
  and and_11 (and_11_out, dec_5_1_1_out_12, Enable);
  and and_12 (and_12_out, dec_5_1_1_out_13, Enable);
  and and_13 (and_13_out, dec_5_1_1_out_14, Enable);
  and and_14 (and_14_out, dec_5_1_1_out_15, Enable);
  and and_15 (and_15_out, dec_5_1_1_out_16, Enable);
  and and_16 (and_16_out, dec_5_1_1_out_17, Enable);
  and and_17 (and_17_out, dec_5_1_1_out_18, Enable);
  and and_18 (and_18_out, dec_5_1_1_out_19, Enable);
  and and_19 (and_19_out, dec_5_1_1_out_20, Enable);
  and and_20 (and_20_out, dec_5_1_1_out_21, Enable);
  and and_21 (and_21_out, dec_5_1_1_out_22, Enable);
  and and_22 (and_22_out, dec_5_1_1_out_23, Enable);
  and and_23 (and_23_out, dec_5_1_1_out_24, Enable);
  and and_24 (and_24_out, dec_5_1_1_out_25, Enable);
  and and_25 (and_25_out, dec_5_1_1_out_26, Enable);
  and and_26 (and_26_out, dec_5_1_1_out_27, Enable);
  and and_27 (and_27_out, dec_5_1_1_out_28, Enable);
  and and_28 (and_28_out, dec_5_1_1_out_29, Enable);
  and and_29 (and_29_out, dec_5_1_1_out_30, Enable);
  and and_30 (and_30_out, dec_5_1_1_out_31, Enable);
  and and_31 (and_31_out, dec_5_1_1_out_32, Enable);
  and and_32 (and_32_out, dec_5_1_1_out_33, Enable);
  Register #(.width(32)) _0 (.D(Write_Data), .en(and_1_out), .clk(Clock), .clr(Reset));  // open: Q
  Register #(.width(32)) register_1 (.D(Write_Data), .en(and_2_out), .Q(register_1_q), .clk(Clock), .clr(Reset));
  Register #(.width(32)) _2 (.D(Write_Data), .en(and_3_out), .Q(_2_q), .clk(Clock), .clr(Reset));
  Register #(.width(32)) _3 (.D(Write_Data), .en(and_4_out), .Q(_3_q), .clk(Clock), .clr(Reset));
  Register #(.width(32)) _4 (.D(Write_Data), .en(and_5_out), .Q(_4_q), .clk(Clock), .clr(Reset));
  Register #(.width(32)) _5 (.D(Write_Data), .en(and_6_out), .Q(_5_q), .clk(Clock), .clr(Reset));
  Register #(.width(32)) _6 (.D(Write_Data), .en(and_7_out), .Q(_6_q), .clk(Clock), .clr(Reset));
  Register #(.width(32)) _7 (.D(Write_Data), .en(and_8_out), .Q(_7_q), .clk(Clock), .clr(Reset));
  Register #(.width(32)) _8 (.D(Write_Data), .en(and_9_out), .Q(_8_q), .clk(Clock), .clr(Reset));
  Register #(.width(32)) _9 (.D(Write_Data), .en(and_10_out), .Q(_9_q), .clk(Clock), .clr(Reset));
  Register #(.width(32)) _10 (.D(Write_Data), .en(and_11_out), .Q(_10_q), .clk(Clock), .clr(Reset));
  Register #(.width(32)) _11 (.D(Write_Data), .en(and_12_out), .Q(_11_q), .clk(Clock), .clr(Reset));
  Register #(.width(32)) _12 (.D(Write_Data), .en(and_13_out), .Q(_12_q), .clk(Clock), .clr(Reset));
  Register #(.width(32)) _13 (.D(Write_Data), .en(and_14_out), .Q(_13_q), .clk(Clock), .clr(Reset));
  Register #(.width(32)) _14 (.D(Write_Data), .en(and_15_out), .Q(_14_q), .clk(Clock), .clr(Reset));
  Register #(.width(32)) _15 (.D(Write_Data), .en(and_16_out), .Q(_15_q), .clk(Clock), .clr(Reset));
  Register #(.width(32)) _16 (.D(Write_Data), .en(and_17_out), .Q(_16_q), .clk(Clock), .clr(Reset));
  Register #(.width(32)) _17 (.D(Write_Data), .en(and_18_out), .Q(_17_q), .clk(Clock), .clr(Reset));
  Register #(.width(32)) _18 (.D(Write_Data), .en(and_19_out), .Q(_18_q), .clk(Clock), .clr(Reset));
  Register #(.width(32)) _19 (.D(Write_Data), .en(and_20_out), .Q(_19_q), .clk(Clock), .clr(Reset));
  Register #(.width(32)) _20 (.D(Write_Data), .en(and_21_out), .Q(_20_q), .clk(Clock), .clr(Reset));
  Register #(.width(32)) _21 (.D(Write_Data), .en(and_22_out), .Q(_21_q), .clk(Clock), .clr(Reset));
  Register #(.width(32)) _22 (.D(Write_Data), .en(and_23_out), .Q(_22_q), .clk(Clock), .clr(Reset));
  Register #(.width(32)) _23 (.D(Write_Data), .en(and_24_out), .Q(_23_q), .clk(Clock), .clr(Reset));
  Register #(.width(32)) _24 (.D(Write_Data), .en(and_25_out), .Q(_24_q), .clk(Clock), .clr(Reset));
  Register #(.width(32)) _25 (.D(Write_Data), .en(and_26_out), .Q(_25_q), .clk(Clock), .clr(Reset));
  Register #(.width(32)) _26 (.D(Write_Data), .en(and_27_out), .Q(_26_q), .clk(Clock), .clr(Reset));
  Register #(.width(32)) _27 (.D(Write_Data), .en(and_28_out), .Q(_27_q), .clk(Clock), .clr(Reset));
  Register #(.width(32)) _28 (.D(Write_Data), .en(and_29_out), .Q(_28_q), .clk(Clock), .clr(Reset));
  Register #(.width(32)) _29 (.D(Write_Data), .en(and_30_out), .Q(_29_q), .clk(Clock), .clr(Reset));
  Register #(.width(32)) _30 (.D(Write_Data), .en(and_31_out), .Q(_30_q), .clk(Clock), .clr(Reset));
  Register #(.width(32)) _31 (.D(Write_Data), .en(and_32_out), .Q(_31_q), .clk(Clock), .clr(Reset));
  Multiplexer #(.select(4), .width(32), .enable("false")) multiplexer_1 (
    .in0({32{1'b0}}), .in1(register_1_q), .in2(_2_q), .in3(_3_q), .in4(_4_q), .in5(_5_q), .in6(_6_q),
    .in7(_7_q), .in8(_8_q), .in9(_9_q), .in10(_10_q), .in11(_11_q), .in12(_12_q), .in13(_13_q), .in14(_14_q),
    .in15(_15_q), .out(multiplexer_1_out), .sel(Read_2_Address[3:0]));
  Multiplexer #(.select(4), .width(32), .enable("false")) multiplexer_2 (
    .in0({32{1'b0}}), .in1(register_1_q), .in2(_2_q), .in3(_3_q), .in4(_4_q), .in5(_5_q), .in6(_6_q),
    .in7(_7_q), .in8(_8_q), .in9(_9_q), .in10(_10_q), .in11(_11_q), .in12(_12_q), .in13(_13_q), .in14(_14_q),
    .in15(_15_q), .out(multiplexer_2_out), .sel(Read_1_Address[3:0]));
  Multiplexer #(.select(4), .width(32), .enable("false")) multiplexer_3 (
    .in0(_16_q), .in1(_17_q), .in2(_18_q), .in3(_19_q), .in4(_20_q), .in5(_21_q), .in6(_22_q), .in7(_23_q),
    .in8(_24_q), .in9(_25_q), .in10(_26_q), .in11(_27_q), .in12(_28_q), .in13(_29_q), .in14(_30_q),
    .in15(_31_q), .out(multiplexer_3_out), .sel(Read_1_Address[3:0]));
  Multiplexer #(.select(4), .width(32), .enable("false")) multiplexer_4 (
    .in0(_16_q), .in1(_17_q), .in2(_18_q), .in3(_19_q), .in4(_20_q), .in5(_21_q), .in6(_22_q), .in7(_23_q),
    .in8(_24_q), .in9(_25_q), .in10(_26_q), .in11(_27_q), .in12(_28_q), .in13(_29_q), .in14(_30_q),
    .in15(_31_q), .out(multiplexer_4_out), .sel(Read_2_Address[3:0]));
  Multiplexer #(.width(32), .enable("false")) multiplexer_5 (
    .in0(multiplexer_2_out), .in1(multiplexer_3_out), .out(Read_Data_1), .sel(Read_1_Address[4]));
  Multiplexer #(.width(32), .enable("false")) multiplexer_6 (
    .in0(multiplexer_1_out), .in1(multiplexer_4_out), .out(Read_Data_2), .sel(Read_2_Address[4]));
endmodule

module Dec_5_1 (
  input  [4:0] in_1,
  output out_2,
  output out_3,
  output out_4,
  output out_5,
  output out_6,
  output out_7,
  output out_8,
  output out_9,
  output out_10,
  output out_11,
  output out_12,
  output out_13,
  output out_14,
  output out_15,
  output out_16,
  output out_17,
  output out_18,
  output out_19,
  output out_20,
  output out_21,
  output out_22,
  output out_23,
  output out_24,
  output out_25,
  output out_26,
  output out_27,
  output out_28,
  output out_29,
  output out_30,
  output out_31,
  output out_32,
  output out_33
);

  wire decoder_1_out0, decoder_2_out0, not_1_out, not_2_out, not_3_out, not_4_out;
  wire [3:0] and_1_out, and_5_out;

  not not_1 (not_1_out, in_1[4]);
  not not_2 (not_2_out, in_1[4]);
  not not_3 (not_3_out, in_1[4]);
  not not_4 (not_4_out, in_1[4]);
  and and_1 (and_1_out[0], not_1_out, in_1[0]);
  and and_2 (and_1_out[1], not_2_out, in_1[1]);
  and and_3 (and_1_out[2], not_3_out, in_1[2]);
  and and_4 (and_1_out[3], not_4_out, in_1[3]);
  and and_5 (and_5_out[0], in_1[4], in_1[0]);
  and and_6 (and_5_out[1], in_1[4], in_1[1]);
  and and_7 (and_5_out[2], in_1[4], in_1[2]);
  and and_8 (and_5_out[3], in_1[4], in_1[3]);
  Decoder #(.select(4), .enable("false")) decoder_1 (
    .out0(decoder_1_out0), .out1(out_3), .out2(out_4), .out3(out_5), .out4(out_6), .out5(out_7),
    .out6(out_8), .out7(out_9), .out8(out_10), .out9(out_11), .out10(out_12), .out11(out_13), .out12(out_14),
    .out13(out_15), .out14(out_16), .out15(out_17), .sel(and_1_out));
  Decoder #(.select(4), .enable("false")) decoder_2 (
    .out0(decoder_2_out0), .out1(out_19), .out2(out_20), .out3(out_21), .out4(out_22), .out5(out_23),
    .out6(out_24), .out7(out_25), .out8(out_26), .out9(out_27), .out10(out_28), .out11(out_29),
    .out12(out_30), .out13(out_31), .out14(out_32), .out15(out_33), .sel(and_5_out));
  and and_9 (out_2, not_1_out, decoder_1_out0);
  and and_10 (out_18, in_1[4], decoder_2_out0);
endmodule

module ALU (
  input  [31:0] in_1,
  input  [31:0] in_2,
  input  [3:0] in_3,
  output Zero,
  output [31:0] out_5
);

  wire comparator_1_lt, comparator_2_eq, comparator_2_gt, not_1_out, or_1_out, or_3_out, or_4_out, or_5_out,
       or_6_out, or_7_out;
  wire [31:0] adder_1_out, and_1_out, bit_extender_1_out, bit_extender_2_out, multiplier_1_out, or_2_out,
       subtractor_1_out;

  Comparator #(.width(32), .mode("unsigned")) comparator_1 (.a(in_1), .b(in_2), .lt(comparator_1_lt));  // open: gt, eq
  Comparator #(.width(32)) comparator_2 (.a(in_1), .b(in_2), .gt(comparator_2_gt), .eq(comparator_2_eq));  // open: lt
  or or_1 (or_1_out, comparator_2_gt, comparator_2_eq);
  not not_1 (not_1_out, or_1_out);
  assign and_1_out = in_1 & in_2;  // AND_Gate and_1, 32 bits wide
  assign or_2_out = in_1 | in_2;  // OR_Gate or_2, 32 bits wide
  Adder #(.width(32)) adder_1 (.a(in_1), .b(in_2), .out(adder_1_out));  // open: cin, cout
  Subtractor #(.width(32)) subtractor_1 (.a(in_1), .b(in_2), .out(subtractor_1_out));  // open: bin, bout
  Multiplier #(.width(32)) multiplier_1 (.a(in_1), .b(in_2), .out(multiplier_1_out));  // open: cin, cout
  assign bit_extender_1_out = {{31{1'b0}}, comparator_1_lt};  // Bit_Extender bit_extender_1
  assign bit_extender_2_out = {{31{1'b0}}, not_1_out};  // Bit_Extender bit_extender_2
  Multiplexer #(.select(4), .width(32), .enable("false")) multiplexer_1 (
    .in0(and_1_out), .in1(or_2_out), .in2(adder_1_out), .in3(multiplier_1_out), .in4(bit_extender_1_out),
    .in6(subtractor_1_out), .in14(bit_extender_2_out), .in15(in_2), .out(out_5), .sel(in_3));  // open: in5, in7, in8, in9, in10, in11, in12, in13
  or or_3 (or_3_out, out_5[0], out_5[1], out_5[2], out_5[3], out_5[4], out_5[5], out_5[6], out_5[7], out_5[8]);
  or or_4 (or_4_out, out_5[9], out_5[10], out_5[11], out_5[12], out_5[13], out_5[14], out_5[15], out_5[16], out_5[17]);
  or or_5 (or_5_out, out_5[18], out_5[19], out_5[20], out_5[21], out_5[22], out_5[23], out_5[24], out_5[25], out_5[26]);
  or or_6 (or_6_out, out_5[27], out_5[28], out_5[29], out_5[30], out_5[31]);
  or or_7 (or_7_out, or_3_out, or_4_out, or_5_out, or_6_out);
  not not_2 (Zero, or_7_out);

  // Notes on the sheet:
  //   Unsigned
  //   Signed
  //   BGE
  //   LUI
  //   MUL
  //   SLTIU
endmodule

module merge_PC (
  input  [27:0] in_1,
  input  [3:0] in_2,
  output [31:0] out_3
);


  assign out_3 = {in_2, in_1};
endmodule

module sig_ext (
  input  [15:0] in_1,
  output [31:0] out_2
);


  assign out_2 = {{17{in_1[15]}}, in_1[14:0]};
endmodule

module ALU_Control (
  input  [1:0] ALUOp,
  input  [2:0] funct3,
  input  [6:0] funct7,
  output [3:0] ALUControl
);

  wire [1:0] bitselector_1_out;
  wire [3:0] multiplexer_1_out, multiplexer_2_out, multiplexer_3_out;

  BitSelector #(.width(7)) bitselector_1 (.in(funct7), .out(bitselector_1_out[0]), .sel(3'b000));
  BitSelector #(.width(7)) bitselector_2 (.in(funct7), .out(bitselector_1_out[1]), .sel(3'b101));
  Multiplexer #(.select(2), .width(4), .enable("false")) multiplexer_1 (
    .in0(4'b0010), .in1(4'b0011), .in2(4'b0110), .in3(4'b0000), .out(multiplexer_1_out),
    .sel(bitselector_1_out));
  Multiplexer #(.select(3), .width(4), .enable("false")) multiplexer_2 (
    .in0(multiplexer_1_out), .in1(4'b0101), .in3(4'b0100), .in5(4'b1110), .in6(4'b0001), .in7(4'b0000),
    .out(multiplexer_2_out), .sel(funct3));  // open: in2, in4
  Multiplexer #(.select(3), .width(4), .enable("false")) multiplexer_3 (
    .in0(4'b0110), .in5(4'b1110), .out(multiplexer_3_out), .sel(funct3));  // open: in1, in2, in3, in4, in6, in7
  Multiplexer #(.select(2), .width(4), .enable("false")) multiplexer_4 (
    .in0(4'b0010), .in1(multiplexer_3_out), .in2(multiplexer_2_out), .in3(4'b1111), .out(ALUControl),
    .sel(ALUOp));
endmodule

module Debug_Register_Bank (
  input  Debug,
  input  Debug_Enable,
  input  [4:0] Debug_Write_Address,
  input  [31:0] Debug_Write_Data,
  input  [4:0] Read_1_Address,
  input  [4:0] Read_2_Address,
  input  [4:0] Write_Address,
  input  [31:0] Write_Data,
  input  Enable,
  input  Reset,
  input  Clock,
  output [31:0] Read_Data_1,
  output [31:0] Read_Data_2
);

  wire and_1_out, not_1_out, or_1_out;
  wire [4:0] multiplexer_1_out;
  wire [31:0] multiplexer_2_out;

  not not_1 (not_1_out, Debug);
  Multiplexer #(.width(5), .enable("false")) multiplexer_1 (
    .in0(Write_Address), .in1(Debug_Write_Address), .out(multiplexer_1_out), .sel(Debug));
  Multiplexer #(.width(32), .enable("false")) multiplexer_2 (
    .in0(Write_Data), .in1(Debug_Write_Data), .out(multiplexer_2_out), .sel(Debug));
  or or_1 (or_1_out, Debug_Enable, Enable);
  and and_1 (and_1_out, not_1_out, Reset);
  Register_Bank register_bank_1 (
    .Read_1_Address(Read_1_Address), .Read_2_Address(Read_2_Address), .Write_Address(multiplexer_1_out),
    .Write_Data(multiplexer_2_out), .Enable(or_1_out), .Reset(and_1_out), .Clock(Clock),
    .Read_Data_1(Read_Data_1), .Read_Data_2(Read_Data_2));
endmodule

module FSM_ROM (
  input  [6:0] OPCode,
  input  Clock,
  input  Reset,
  input  PCWriteCond,
  input  PCWrite,
  input  IorD,
  input  MemRead,
  input  MemWrite,
  input  MemToReg,
  input  IRWrite,
  input  RegWrite,
  input  [1:0] ALUsrcA,
  input  [1:0] ALUsrcB,
  input  [1:0] ALUop,
  input  PCSource,
  input  Debug,
  output PCWriteCond_2,
  output PCWrite_2,
  output IorD_2,
  output MemRead_2,
  output MemWrite_2,
  output [3:0] Estado__debug,
  output MemtoReg_2,
  output IRWrite_2,
  output RegWrite_2,
  output [1:0] ALUSrcA_2,
  output [1:0] ALUSrcB_2,
  output [1:0] ALUop_2,
  output PCSource_2
);

  wire [3:0] rom_2_data;
  wire [14:0] rom_1_data;

  ROM #(.addrWidth(4), .dataWidth(15)) rom_1 (.addr(Estado__debug), .data(rom_1_data), .sel(1'b1));
  ROM #(.addrWidth(11), .dataWidth(4)) rom_2 (.addr({OPCode, Estado__debug}), .data(rom_2_data), .sel(1'b1));
  Register #(.width(4)) Current_State (.D(rom_2_data), .en(1'b1), .Q(Estado__debug), .clk(Clock), .clr(Reset));
  Multiplexer #(.enable("false")) multiplexer_1 (
    .in0(rom_1_data[0]), .in1(PCWriteCond), .out(PCWriteCond_2), .sel(Debug));
  Multiplexer #(.enable("false")) multiplexer_2 (.in0(rom_1_data[1]), .in1(PCWrite), .out(PCWrite_2), .sel(Debug));
  Multiplexer #(.enable("false")) multiplexer_3 (.in0(rom_1_data[2]), .in1(IorD), .out(IorD_2), .sel(Debug));
  Multiplexer #(.enable("false")) multiplexer_4 (.in0(rom_1_data[3]), .in1(MemRead), .out(MemRead_2), .sel(Debug));
  Multiplexer #(.enable("false")) multiplexer_5 (.in0(rom_1_data[4]), .in1(MemWrite), .out(MemWrite_2), .sel(Debug));
  Multiplexer #(.enable("false")) multiplexer_6 (.in0(rom_1_data[5]), .in1(MemToReg), .out(MemtoReg_2), .sel(Debug));
  Multiplexer #(.enable("false")) multiplexer_7 (.in0(rom_1_data[6]), .in1(IRWrite), .out(IRWrite_2), .sel(Debug));
  Multiplexer #(.enable("false")) multiplexer_8 (.in0(rom_1_data[7]), .in1(RegWrite), .out(RegWrite_2), .sel(Debug));
  Multiplexer #(.width(2), .enable("false")) multiplexer_9 (
    .in0(rom_1_data[9:8]), .in1(ALUsrcA), .out(ALUSrcA_2), .sel(Debug));
  Multiplexer #(.width(2), .enable("false")) multiplexer_10 (
    .in0(rom_1_data[11:10]), .in1(ALUsrcB), .out(ALUSrcB_2), .sel(Debug));
  Multiplexer #(.width(2), .enable("false")) multiplexer_11 (
    .in0(rom_1_data[13:12]), .in1(ALUop), .out(ALUop_2), .sel(Debug));
  Multiplexer #(.enable("false")) multiplexer_12 (.in0(rom_1_data[14]), .in1(PCSource), .out(PCSource_2), .sel(Debug));

  // Notes on the sheet:
  //   ROM de saída:
  //   ROM de próximo estado
  //   S0 = 0x044a fetch
  //   S5 = 0x0014 store
  //   S8 = 0x5201 branch
  //   opcode (7bits) + estado (4bits)
  //   LUI -  0x370 -> 0x1, 0x371 ->0xA, 0x37A -> 0x7
  //   S2 = 0x0A00 calc endereço load/store
  //   S3 = 0x000C leitura de memória
  //   S4 = 0x00A0 writeback de load
  //   S6 = 0x2200 execute R-type
  //   S7 = 0x0080 writeback ALU
  //   SA = 0x3800 execute do U-type/LUI
  //   S1 = 0x0D00 decode ALUSrcA=01 ALUSrcB=11 ALUOp=00
  //   Geração da saída
  //   opcode + estado
  //   Próximo Estado
  //   contents of rom_1 (hex, n*v repeats v):
  //   44a d00 a00 c a0 14 2200 80 5201 2a00 3800 0 500 a82
  //   contents of rom_2 (hex, n*v repeats v):
  //   1 47*0 1 2 3 4 252*0 1 9 7*0 7 246*0 1 2 5 253*0 1 6 4*0 7 57*0 1 a 7 7*0 7 693*0 1 8 62*0 1 c 10*0
  //   d
endmodule

module ImmGen (
  input  [31:0] Instruction,
  output [31:0] Immediate
);

  wire [2:0] rom_1_data;
  wire [31:0] B_Type, I_Type, S_Type;

  // Probe on Instruction[6:0]
  assign B_Type = {{20{Instruction[31]}}, {Instruction[31], Instruction[7], Instruction[30:25], Instruction[11:8]}};  // Bit_Extender bit_extender_1
  assign S_Type = {{20{Instruction[31]}}, {Instruction[31:25], Instruction[11:7]}};  // Bit_Extender bit_extender_2
  assign I_Type = {{20{Instruction[31]}}, Instruction[31:20]};  // Bit_Extender bit_extender_3
  ROM #(.addrWidth(7), .dataWidth(3)) rom_1 (.addr(Instruction[6:0]), .data(rom_1_data));  // open: sel
  Multiplexer #(.select(3), .width(32), .enable("false")) multiplexer_1 (
    .in0(I_Type), .in1(S_Type), .in2(B_Type), .in3({Instruction[31:12], {12{1'b0}}}), .out(Immediate),
    .sel(rom_1_data));  // open: in4, in5, in6, in7

  // Other names for the same wires on the sheet: opcode[6:0] = Instruction[6:0]; U_Type[31:12] = Instruction[31:12]

  // Notes on the sheet:
  //   contents of rom_1 (hex, n*v repeats v):
  //   35*0 1 19*0 3 43*0 2 11*0 4
endmodule

module postALU (
  input  [6:0] opcode,
  input  [31:0] ALU_Computed_Address,
  output [31:0] Final_Address
);

  wire comparator_1_eq;
  wire [31:0] and_1_out, not_1_out;

  Comparator #(.width(7), .mode("unsigned")) comparator_1 (
    .a(opcode), .b(7'b1100111), .eq(comparator_1_eq));  // open: gt, lt
  assign not_1_out = ~32'h1;  // NOT_Gate not_1, 32 bits wide
  Multiplexer #(.width(32), .enable("false")) multiplexer_1 (
    .in0(ALU_Computed_Address), .in1(and_1_out), .out(Final_Address), .sel(comparator_1_eq));
  assign and_1_out = ALU_Computed_Address & not_1_out;  // AND_Gate and_1, 32 bits wide
endmodule
